# Fritzing sketch LCD_transition_days_circuit (saved by Fritzing 0.9.6b)
stripboards: 1
breadboards: 1

parts:
  LCD1 = Adafruit Positive RGB 2x16 LCD
  R1 = Resistor [tolerance=±5% power=0.25 resistance=220 package=THT]
  R2 = Resistor [tolerance=±5% power=0.25 resistance=220 package=THT]
  R3 = Resistor [tolerance=±5% power=0.25 resistance=220 package=THT]
  R4 = Rotary Potentiometer (Small) [maximum_resistance=10kΩ package=THT]
  Arduino = Arduino Uno (Rev3)

nets (from the schematic view):
  N1: LCD1.no_name_yet#0, LCD1.no_name_yet#4, R4.leg1, Arduino.GND
  N2: LCD1.no_name_yet#1, LCD1.no_name_yet#14, R4.leg2, Arduino.5V
  N3: LCD1.no_name_yet#2, R4.wiper
  N4: LCD1.no_name_yet#3, Arduino.D7
  N5: LCD1.no_name_yet#5, Arduino.D6_PWM
  N6: LCD1.no_name_yet#10, Arduino.D5_PWM
  N7: LCD1.no_name_yet#11, Arduino.D4
  N8: LCD1.no_name_yet#12, Arduino.D3_PWM
  N9: LCD1.no_name_yet#13, Arduino.D2
  N10: LCD1.no_name_yet#15, R3.Pin_1
  N11: LCD1.no_name_yet#16, R2.Pin_1
  N12: LCD1.no_name_yet#17, R1.Pin_1
  N13: R1.Pin_0, Arduino.D11_PWM/MOSI
  N14: R2.Pin_0, Arduino.D10_PWM/SS
  N15: R3.Pin_0, Arduino.D9_PWM

notes:
  wires to cut

custom parts:
  Adafruit Positive RGB 2x16 LCD: Adafruit Positive 2x16 LCD Display with RGB Backlight
